// Logisim project 8bitPC.circ as structural Verilog: 1 circuit, main circuit main
module main (
  input  CLEAR,
  input  reset
);

  wire and_1_out, and_2_out, bcd_to_7_segment_decoder_5_p1, binary_to_bcd_converter_1_p2,
       binary_to_bcd_converter_1_p4, clock_1_out, n7_segment_display_3_p1, n7_segment_display_4_p1,
       n7_segment_display_6_p1, or_1_out, or_2_out, or_3_out;
  wire [2:0] and_3_out, FR_q;
  wire [3:0] IX_q, ledbar_1_p1_2, PC_q;
  wire [6:0] controlled_buffer_11_out, keyboard_1_data, ledbar_1_p1;
  wire [7:0] adder_1_out, AX_q, bit_extender_2_out, bit_extender_3_out, bit_extender_4_out, BX_q,
       controlled_buffer_1_out, controlled_buffer_2_out, controlled_buffer_3_out, controlled_buffer_4_out,
       controlled_buffer_7_out, controlled_buffer_14_out, ledbar_2_p1, ram_1_data, RNDGen_out, xor_8_out;
  wire [7:7] controlled_buffer_11_out_2;
  wire [15:0] PRIMARY_MICROCODE_data, SECONDARY_MICROCODE_data;

  // LedBar #(.inputtype("row"), .matrixcols(11)) ledbar_1: pin names not known; wires that end beside it: {ledbar_1_p1_2, ledbar_1_p1}
  Counter #(.max('hf), .width(4)) counter_1 (
    .clr(reset), .load(SECONDARY_MICROCODE_data[14]), .up(1'b1), .count(PRIMARY_MICROCODE_data[1]),
    .clk(and_2_out), .D(controlled_buffer_4_out[3:0]), .Q(ledbar_2_p1[7:4]));  // open: carry
  Clock clock_1 (.out(clock_1_out));
  or or_1 (or_1_out, reset, PRIMARY_MICROCODE_data[1]);
  Counter #(.max('hf), .width(4)) PC (
    .clr(or_1_out), .load(PRIMARY_MICROCODE_data[8]), .up(1'b1), .count(PRIMARY_MICROCODE_data[7]),
    .clk(and_2_out), .D(controlled_buffer_1_out[3:0]), .Q(PC_q));  // open: carry
  // LedBar #(.inputtype("row")) ledbar_2: pin names not known; wires that end beside it: ledbar_2_p1
  assign ledbar_1_p1_2 = {{1{1'b0}}, FR_q};  // Bit_Extender bit_extender_1
  and and_1 (and_1_out, clock_1_out, ~reset);  // AND_Gate
  ROM #(.addrWidth(11), .dataWidth(16)) SECONDARY_MICROCODE (
    .addr({ledbar_1_p1_2, ledbar_1_p1}), .data(SECONDARY_MICROCODE_data));
  and and_2 (and_2_out, and_1_out, ~PRIMARY_MICROCODE_data[0]);  // AND_Gate
  RAM #(.asyncread("true"), .databus("bidir")) ram_1 (
    .addr(ledbar_2_p1), .we(PRIMARY_MICROCODE_data[4]), .oe(PRIMARY_MICROCODE_data[5]), .clk(and_2_out),
    .data(ram_1_data));
  Register IX (
    .D(controlled_buffer_3_out), .en(PRIMARY_MICROCODE_data[10]), .clk(and_2_out),
    .Q({ledbar_1_p1[6:3], IX_q}), .clr(reset));
  // LedBar #(.inputtype("row")) ledbar_3: pin names not known; wires that end beside it: {ledbar_1_p1[6:3], IX_q}
  Counter #(.max('h4), .trigger("falling"), .width(3)) StepCTR (
    .clr(reset), .up(1'b1), .count(1'b1), .clk(and_2_out), .Q(ledbar_1_p1[2:0]));  // open: load, D, carry
  Register #(.width(4)) MX (
    .D(controlled_buffer_2_out[3:0]), .en(PRIMARY_MICROCODE_data[6]), .clk(and_2_out), .Q(ledbar_2_p1[3:0]),
    .clr(reset));
  // LedBar #(.inputtype("row"), .matrixcols(4)) ledbar_4: pin names not known; wires that end beside it: ledbar_2_p1[7:4]
  assign bit_extender_2_out = {{4{1'b0}}, PC_q};  // Bit_Extender bit_extender_2
  assign controlled_buffer_1_out = PRIMARY_MICROCODE_data[8] ? ram_1_data : 8'bz;  // Controlled_Buffer controlled_buffer_1
  assign controlled_buffer_2_out = PRIMARY_MICROCODE_data[6] ? ram_1_data : 8'bz;  // Controlled_Buffer controlled_buffer_2
  // LedBar #(.inputtype("row"), .matrixcols(4)) ledbar_5: pin names not known; wires that end beside it: ledbar_2_p1[3:0]
  assign controlled_buffer_3_out = PRIMARY_MICROCODE_data[10] ? ram_1_data : 8'bz;  // Controlled_Buffer controlled_buffer_3
  assign bit_extender_3_out = {{4{1'b0}}, IX_q};  // Bit_Extender bit_extender_3
  Pull_Resistor pull_resistor_1 (.node(SECONDARY_MICROCODE_data));
  assign controlled_buffer_4_out = SECONDARY_MICROCODE_data[14] ? ram_1_data : 8'bz;  // Controlled_Buffer controlled_buffer_4
  assign bit_extender_4_out = {{1{1'b0}}, keyboard_1_data};  // Bit_Extender bit_extender_4
  // LedBar #(.inputtype("row")) ledbar_6: pin names not known; wires that end beside it: ram_1_data
  assign ram_1_data = PRIMARY_MICROCODE_data[15] ? AX_q : 8'bz;  // Controlled_Buffer controlled_buffer_5
  assign ram_1_data = PRIMARY_MICROCODE_data[9] ? bit_extender_2_out : 8'bz;  // Controlled_Buffer controlled_buffer_6
  assign controlled_buffer_7_out = PRIMARY_MICROCODE_data[14] ? ram_1_data : 8'bz;  // Controlled_Buffer controlled_buffer_7
  assign ram_1_data = PRIMARY_MICROCODE_data[3] ? adder_1_out : 8'bz;  // Controlled_Buffer controlled_buffer_8
  assign ram_1_data = PRIMARY_MICROCODE_data[11] ? bit_extender_3_out : 8'bz;  // Controlled_Buffer controlled_buffer_9
  ROM #(.addrWidth(11), .dataWidth(16)) PRIMARY_MICROCODE (
    .addr({ledbar_1_p1_2, ledbar_1_p1}), .data(PRIMARY_MICROCODE_data));
  assign ram_1_data = SECONDARY_MICROCODE_data[13] ? RNDGen_out : 8'bz;  // Controlled_Buffer controlled_buffer_10
  assign {controlled_buffer_11_out_2[7], controlled_buffer_11_out} = SECONDARY_MICROCODE_data[12] ? ram_1_data : 8'bz;  // Controlled_Buffer controlled_buffer_11
  assign ram_1_data = SECONDARY_MICROCODE_data[9] ? bit_extender_4_out : 8'bz;  // Controlled_Buffer controlled_buffer_12
  xor xor_1 (xor_8_out[7], BX_q[7], PRIMARY_MICROCODE_data[2]);
  assign ram_1_data = PRIMARY_MICROCODE_data[13] ? BX_q : 8'bz;  // Controlled_Buffer controlled_buffer_13
  assign controlled_buffer_14_out = PRIMARY_MICROCODE_data[12] ? ram_1_data : 8'bz;  // Controlled_Buffer controlled_buffer_14
  xor xor_2 (xor_8_out[6], BX_q[6], PRIMARY_MICROCODE_data[2]);
  xor xor_3 (xor_8_out[5], BX_q[5], PRIMARY_MICROCODE_data[2]);
  xor xor_4 (xor_8_out[4], BX_q[4], PRIMARY_MICROCODE_data[2]);
  xor xor_5 (xor_8_out[3], BX_q[3], PRIMARY_MICROCODE_data[2]);
  Random RNDGen (.clr(reset), .next(SECONDARY_MICROCODE_data[13]), .clk(and_2_out), .out(RNDGen_out));
  TTY tty_1 (.data(controlled_buffer_11_out), .clk(and_2_out), .we(SECONDARY_MICROCODE_data[12]), .clr(or_2_out));
  Keyboard keyboard_1 (
    .clk(and_2_out), .re(SECONDARY_MICROCODE_data[9]), .clr(or_3_out), .avail(and_3_out[2]),
    .data(keyboard_1_data));
  or or_2 (or_2_out, SECONDARY_MICROCODE_data[11], CLEAR);
  Register AX (.D(controlled_buffer_7_out), .en(PRIMARY_MICROCODE_data[14]), .clk(and_2_out), .Q(AX_q), .clr(reset));
  xor xor_6 (xor_8_out[2], BX_q[2], PRIMARY_MICROCODE_data[2]);
  xor xor_7 (xor_8_out[1], BX_q[1], PRIMARY_MICROCODE_data[2]);
  Register BX (.D(controlled_buffer_14_out), .en(PRIMARY_MICROCODE_data[12]), .clk(and_2_out), .Q(BX_q), .clr(reset));
  Pull_Resistor pull_resistor_2 (.node(PRIMARY_MICROCODE_data));
  or or_3 (or_3_out, SECONDARY_MICROCODE_data[10], CLEAR);
  // LedBar #(.inputtype("row")) ledbar_7: pin names not known; wires that end beside it: AX_q
  xor xor_8 (xor_8_out[0], BX_q[0], PRIMARY_MICROCODE_data[2]);
  _7_Segment_Display u_7_segment_display_1 ();  // open: g, f, a, b, e, d, c, dp
  // BCD_to_7_Segment_decoder bcd_to_7_segment_decoder_1: pin names not known
  // Binary_to_BCD_converter #(.binvalue(8)) binary_to_bcd_converter_1: pin names not known; wires that end beside it: AX_q, binary_to_bcd_converter_1_p2, binary_to_bcd_converter_1_p2, binary_to_bcd_converter_1_p4
  Adder adder_1 (.a(AX_q), .b(xor_8_out), .out(adder_1_out), .cin(PRIMARY_MICROCODE_data[2]), .cout(and_3_out[1]));
  // LedBar #(.inputtype("row")) ledbar_8: pin names not known; wires that end beside it: BX_q
  _7_Segment_Display u_7_segment_display_2 ();  // open: g, f, a, b, e, d, c, dp
  // BCD_to_7_Segment_decoder bcd_to_7_segment_decoder_2: pin names not known; wires that end beside it: binary_to_bcd_converter_1_p4
  // _7_Segment_Display 7_segment_display_3: pin names not known; wires that end beside it: n7_segment_display_3_p1, n7_segment_display_3_p1
  // _7_Segment_Display 7_segment_display_4: pin names not known; wires that end beside it: n7_segment_display_4_p1, n7_segment_display_4_p1
  // BCD_to_7_Segment_decoder bcd_to_7_segment_decoder_3: pin names not known
  // BCD_to_7_Segment_decoder bcd_to_7_segment_decoder_4: pin names not known
  // Binary_to_BCD_converter #(.binvalue(8)) binary_to_bcd_converter_2: pin names not known; wires that end beside it: BX_q
  _7_Segment_Display u_7_segment_display_5 ();  // open: g, f, a, b, e, d, c, dp
  // BCD_to_7_Segment_decoder bcd_to_7_segment_decoder_5: pin names not known; wires that end beside it: bcd_to_7_segment_decoder_5_p1, bcd_to_7_segment_decoder_5_p1
  and and_3 (and_3_out[0], ~adder_1_out[0], ~adder_1_out[1], ~adder_1_out[2], ~adder_1_out[3], ~adder_1_out[4], ~adder_1_out[5], ~adder_1_out[6], ~adder_1_out[7]);  // AND_Gate
  // _7_Segment_Display 7_segment_display_6: pin names not known; wires that end beside it: n7_segment_display_6_p1, n7_segment_display_6_p1
  // BCD_to_7_Segment_decoder bcd_to_7_segment_decoder_6: pin names not known
  Register #(.width(3)) FR (.D(and_3_out), .en(SECONDARY_MICROCODE_data[15]), .clk(and_2_out), .Q(FR_q), .clr(reset));

  // Notes on the sheet:
  //   contents of SECONDARY_MICROCODE (hex, n*v repeats v):
  //   20*0 8000 7*0 8000 29*0 4000 7*0 2000 23*0 8000 7*0 1000 7*0 c00 41*0 8000 7*0 8000 29*0 4000 7*0
  //   2000 23*0 8000 7*0 1000 7*0 c00 41*0 8000 7*0 8000 29*0 4000 7*0 2000 23*0 8000 7*0 1000 7*0 c00
  //   41*0 8000 7*0 8000 29*0 4000 7*0 2000 23*0 8000 7*0 1000 7*0 c00 41*0 8000 7*0 8000 29*0 4000 7*0
  //   2000 23*0 8200 7*0 1000 7*0 c00 41*0 8000 7*0 8000 29*0 4000 7*0 2000 23*0 8200 7*0 1000 7*0 c00
  //   41*0 8000 7*0 8000 29*0 4000 7*0 2000 23*0 8200 7*0 1000 7*0 c00 41*0 8000 7*0 8000 29*0 4000 7*0
  //   2000 23*0 8200 7*0 1000 7*0 c00
  //   contents of PRIMARY_MICROCODE (hex, n*v repeats v):
  //   240 4a0 6*0 240 4a0 840 4020 4*0 240 4a0 840 1020 4008 0 0 0 240 4a0 840 1020 400c 0 0 0 240 4a0 900
  //   5*0 240 4a0 6*0 240 4a0 6*0 240 4a0 800 5*0 240 4a0 4000 5*0 240 4a0 840 8010 4*0 240 4a0 900 5*0
  //   240 4a0 6*0 240 4a0 8000 5*0 240 4a0 6*0 240 4a0 8002 5*0 240 4a0 1 5*0 240 4a0 6*0 240 4a0 840 4020
  //   4*0 240 4a0 840 1020 4008 0 0 0 240 4a0 840 1020 400c 0 0 0 240 4a0 900 5*0 240 4a0 900 5*0 240 4a0
  //   6*0 240 4a0 800 5*0 240 4a0 4000 5*0 240 4a0 840 8010 4*0 240 4a0 900 5*0 240 4a0 6*0 240 4a0 8000
  //   5*0 240 4a0 6*0 240 4a0 8002 5*0 240 4a0 1 5*0 240 4a0 6*0 240 4a0 840 4020 4*0 240 4a0 840 1020
  //   4008 0 0 0 240 4a0 840 1020 400c 0 0 0 240 4a0 900 5*0 240 4a0 6*0 240 4a0 900 5*0 240 4a0 800 5*0
  //   240 4a0 4000 5*0 240 4a0 840 8010 4*0 240 4a0 900 5*0 240 4a0 6*0 240 4a0 8000 5*0 240 4a0 6*0 240
  //   4a0 8002 5*0 240 4a0 1 5*0 240 4a0 6*0 240 4a0 840 4020 4*0 240 4a0 840 1020 4008 0 0 0 240 4a0 840
  //   1020 400c 0 0 0 240 4a0 900 5*0 240 4a0 900 5*0 240 4a0 900 5*0 240 4a0 800 5*0 240 4a0 4000 5*0 240
  //   4a0 840 8010 4*0 240 4a0 900 5*0 240 4a0 6*0 240 4a0 8000 5*0 240 4a0 6*0 240 4a0 8002 5*0 240 4a0 1
  //   5*0 240 4a0 6*0 240 4a0 840 4020 4*0 240 4a0 840 1020 4008 0 0 0 240 4a0 840 1020 400c 0 0 0 240 4a0
  //   900 5*0 240 4a0 6*0 240 4a0 6*0 240 4a0 800 5*0 240 4a0 4000 5*0 240 4a0 840 8010 4*0 240 4a0 6*0
  //   240 4a0 4000 5*0 240 4a0 8000 5*0 240 4a0 6*0 240 4a0 8002 5*0 240 4a0 1 5*0 240 4a0 6*0 240 4a0 840
  //   4020 4*0 240 4a0 840 1020 4008 0 0 0 240 4a0 840 1020 400c 0 0 0 240 4a0 900 5*0 240 4a0 900 5*0 240
  //   4a0 6*0 240 4a0 800 5*0 240 4a0 4000 5*0 240 4a0 840 8010 4*0 240 4a0 6*0 240 4a0 4000 5*0 240 4a0
  //   8000 5*0 240 4a0 6*0 240 4a0 8002 5*0 240 4a0 1 5*0 240 4a0 6*0 240 4a0 840 4020 4*0 240 4a0 840
  //   1020 4008 0 0 0 240 4a0 840 1020 400c 0 0 0 240 4a0 900 5*0 240 4a0 6*0 240 4a0 900 5*0 240 4a0 800
  //   5*0 240 4a0 4000 5*0 240 4a0 840 8010 4*0 240 4a0 6*0 240 4a0 4000 5*0 240 4a0 8000 5*0 240 4a0 6*0
  //   240 4a0 8002 5*0 240 4a0 1 5*0 240 4a0 6*0 240 4a0 840 4020 4*0 240 4a0 840 1020 4008 0 0 0 240 4a0
  //   840 1020 400c 0 0 0 240 4a0 900 5*0 240 4a0 900 5*0 240 4a0 900 5*0 240 4a0 800 5*0 240 4a0 4000 5*0
  //   240 4a0 840 8010 4*0 240 4a0 6*0 240 4a0 4000 5*0 240 4a0 8000 5*0 240 4a0 6*0 240 4a0 8002 5*0 240
  //   4a0 1
  //   FI
  //   SI
  //   RNDO
  //   TTYOUT
  //   TTYC
  //   KBC
  //   KBO
  //   AO
  //   AI
  //   BO
  //   BI
  //   IO
  //   II
  //   CO
  //   J
  //   CE
  //   MI
  //   RO
  //   RI
  //   ALUO
  //   SUB
  //   NEXT
  //   halt
endmodule
